# Fritzing sketch Circuit (saved by Fritzing 0.9.5d)
breadboards: 2

parts:
  Part3 = TXB0108 8-channel Bi-directional Logic Level Converter
  M1 = WX-DC12003 [package=THT]
  USBTTL1 = Micro USB B Plug  # not connected
  Part4 = Solid State High Level Relay Module [package=relay]
  LED1 = LED - 3mm [color="Red (633nm)" package="3 mm [THT]"]

nets:
  N1: Part3.VCCB, M1.DC_OUT+, Part4.DC+
  N2: Part3.B1, Part4.CH1
  N3: Part3.GND, LED1.cathode
  N4: Part3.VCCA, M1.DC_OUT-, Part4.DC-

notes:
  To AC 110V-220V
  W1 W2 W3 Y1 Y2 G O B
  To 24VAC Power

custom parts:
  TXB0108 8-channel Bi-directional Logic Level Converter: Because the Arduino (and Basic Stamp) are 5V devices, and most modern sensors, displays, flash cards and modes are 3.3V-only, many makers find that they need to perform level shifting/conversion to protect the 3.3V device from 5V. Although one can use resistors to make a divider, for high speed transfers, the resistors can add a lot of slew and cause havoc that is tough to debug. For that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
  WX-DC12003: Ac to DC power supply 110/220V in 5v 700ma or 12 V 300ma out.
  Solid State High Level Relay Module: 5V Omron solid state relay 240V 2A output with resistance fuse.
