# Fritzing sketch CktFreq (saved by Fritzing 0.9.5d)
breadboards: 2

parts:
  M1 = WX-DC12003 [package=THT]
  Part1 = Arduino Pro Mini v13
  U1 = Optocoupler [package=THT]
  R1 = Resistor [tolerance=±5% resistance=100k package="0402 [SMD]"]
  D1 = Diode [package=diode-1n4001]
  R2 = Resistor [tolerance=±5% resistance=12k package="0402 [SMD]"]
  M2 = TTGO-T-Call-V1.3-ESP32 [package=THT]
  LED1 = smd LED [color="Red (633nm)" package="0805 [SMD]"]
  Part3 = I2C level shifter bidirectional

nets:
  N1: M1.DC_OUT+, Part1.RAW, Part1.D2, U1.Pin_5, R2.Pin_0, R2.Pin_1, M2.5V, Part3.HV
  GND: M1.DC_OUT-, Part1.GND, U1.Pin_4, M2.12, LED1.cathode, Part3.GND
  N2: Part1.D6_PWM, Part3.HV1
  N3: Part1.D5_PWM, Part3.HV2
  N4: U1.Pin_1, R1.Pin_0, R1.Pin_1, D1.C
  N5: M2.3V3, Part3.LV
  N6: M2.13, LED1.anode
  N7: M2.RXD, Part3.LV2
  N8: M2.TXD, Part3.LV1

notes:
  To AC 110V-220V
  100k R
  1N4007
  12k R

custom parts:
  WX-DC12003: Ac to DC power supply 110/220V in 5v 700ma or 12 V 300ma out.
  TTGO-T-Call-V1.3-ESP32: LILYGO® TTGO T-Call V1.3 ESP32 Wireless Module GPRS Antenna SIM Card SIM800L Module. This version has breadboard flipped to the bottom of the board!
