# Fritzing sketch Programmer (saved by Fritzing 0.9.5d)
breadboards: 1

parts:
  Part1 = Arduino Pro Mini v13
  Part2 = FTDI Basic Programmer
  USBTTL1 = USB A Plug  # not connected
  USBTTL2 = Micro USB B Plug  # not connected

nets:
  N1: Part1.D0/TX, Part2.RXI
  N2: Part1.D1/RX, Part2.TXO
  GND: Part1.GND, Part2.GND
  N3: Part1.RAW, Part2.POWER

notes:
  To Computer
